# Fritzing sketch Full Schematic (saved by Fritzing 0.9.6b)
breadboards: 2

parts:
  LCD1 = LCD screen
  R1 = Trimmer Potentiometer [maximum_resistance=10kΩ package=THT]
  U1 = 74HC595 [package="DIP16 [THT]"]
  Part1 = Breakout Board for Electret Microphone
  R2 = Resistor [tolerance=±5% resistance=220 package="0805 [SMD]"]
  Part2 = Arduino Uno (Rev3) - ICSP
  IC1 = L293D [package=THT]
  S1 = Pushbutton [package="[SMD]"]
  LED5 = LED - 3mm [color="Green (555nm)" current=0.030 package="3 mm [THT]"]
  R3 = Resistor [tolerance=±5% resistance=220 package="0805 [SMD]"]
  R4 = Resistor [tolerance=±5% resistance=220 package="0805 [SMD]"]
  R5 = Resistor [tolerance=±5% resistance=220 package="0805 [SMD]"]
  R6 = Resistor [tolerance=±5% resistance=220 package="0805 [SMD]"]
  R7 = Resistor [tolerance=±5% resistance=220 package="0805 [SMD]"]
  R8 = Resistor [tolerance=±5% resistance=220 package="0805 [SMD]"]
  LED6 = LED - 3mm [color="Green (555nm)" current=0.030 package="3 mm [THT]"]
  LED7 = LED - 3mm [color="Green (555nm)" current=0.030 package="3 mm [THT]"]
  LED8 = LED - 3mm [color="Green (555nm)" current=0.030 package="3 mm [THT]"]
  LED9 = LED - 3mm [color="Green (555nm)" current=0.030 package="3 mm [THT]"]
  LED10 = LED - 3mm [color="Green (555nm)" current=0.030 package="3 mm [THT]"]
  R9 = Resistor [tolerance=±5% resistance=330 package="0805 [SMD]"]
  VCC1 = Battery block 9V
  VCC2 = Battery
  M1 = DC Motor

nets:
  GND: LCD1.VSS, LCD1.R/W, LCD1.LED-, R1.leg2, U1.OE, Part1.GND, Part2.GND, IC1.0V, LED5.cathode, LED6.cathode, LED7.cathode, LED8.cathode, LED9.cathode, LED10.cathode, R9.Pin_1, VCC1.-, VCC2.-
  VCC: LCD1.VDD, R1.leg1, U1.MR, U1.VCC, Part1.VCC, R2.Pin_1, S1.Pin_3, S1.Pin_4
  N1: LCD1.V0, R1.wiper
  N2: LCD1.RS, U1.Q1
  N3: LCD1.E, U1.Q3
  N4: LCD1.DB4, U1.Q4
  N5: LCD1.DB5, U1.Q5
  N6: LCD1.DB6, U1.Q6
  N7: LCD1.DB7, U1.Q7
  N8: LCD1.LED+, R2.Pin_0
  N9: U1.SH_CP, Part2.D13/SCK
  N10: U1.ST_CP, Part2.D10_PWM/SS
  N11: U1.DS, Part2.D11_PWM/MOSI
  N12: Part1.AUD, Part2.A0
  N13: Part2.A4/SDA, R4.Pin_0
  N14: Part2.A5/SCL, R3.Pin_0
  N15: Part2.D8, IC1.In_1
  N16: Part2.D9_PWM, IC1.Enable_1
  N17: Part2.D12/MISO, IC1.In_2
  N18: Part2.D3_PWM, R5.Pin_0
  N19: Part2.D4, R6.Pin_0
  N20: Part2.D5_PWM, R7.Pin_0
  N21: Part2.D6_PWM, R8.Pin_0
  N22: Part2.D7, S1.Pin_1, S1.Pin_2, R9.Pin_0
  N23: IC1.Out_1_(_Controlled_by_Enable_1_), M1.pin_1
  N24: IC1.Out_2_(_Controlled_by_Enable_1_), M1.pin_2
  N25: IC1.+Vmotor, VCC1.+, VCC2.+
  N26: LED5.anode, R3.Pin_1
  N27: R4.Pin_1, LED10.anode
  N28: R5.Pin_1, LED9.anode
  N29: R6.Pin_1, LED8.anode
  N30: R7.Pin_1, LED7.anode
  N31: R8.Pin_1, LED6.anode
